# Fritzing sketch EspressoBin-Fan-LED (saved by Fritzing 0.9.3b)
circuit board: 1.54744cm x 5.89417cm
perfboards: 1

parts:
  J2 = male pin header, 2 pins [form="♂ (male)"]
  J1 = male pin header, 23 pins [form="♂ (male)"]
  J4 = female pin header, 2 pins [form="♀ (female)"]
  LED1 = RGB LED - (4 legs) [package="5 mm [THT]"]
  U1 = mystery part, 2 pins [chip_label=Fan]
  J5 = female pin header, 4 pins [form="♀ (female)"]
  R4 = Resistor [tolerance=±5% resistance=220 package=THT]
  R5 = Resistor [tolerance=±5% resistance=220 package=THT]
  R6 = Resistor [tolerance=±5% resistance=220 package=THT]
  R8 = Resistor [tolerance=±5% resistance=220 package=THT]
  R1 = Resistor [tolerance=±5% resistance=510 package=THT]
  R2 = Resistor [tolerance=±5% resistance=580 package=THT]
  R3 = Resistor [tolerance=±5% resistance=150 package=THT]
  R9 = Resistor [tolerance=±5% resistance=2.2k package=THT]
  R10 = Resistor [tolerance=±5% resistance=2.2k package=THT]
  R11 = Resistor [tolerance=±5% resistance=2.2k package=THT]
  Q1 = NPN-Transistor [part_number=2N2222 package="TO92 [THT]"]
  Q4 = NPN-Transistor [part_number=2N2222 package="TO92 [THT]"]
  Q3 = NPN-Transistor [part_number=2N2222 package="TO92 [THT]"]
  Q2 = NPN-Transistor [part_number=2N2222 package="TO92 [THT]"]
  J3 = male pin header, 4 pins [form="♂ (male)"]

nets:
  N1: J2.pin1, J1.pin3, J3.pin2
  N2: J2.pin2, Q4.C
  GND: J1.pin1, J1.pin22, R9.Pin_1, R10.Pin_1, R11.Pin_1, Q1.E, Q4.E, Q3.E, Q2.E
  N3: J1.pin10, R8.Pin_0
  N4: J1.pin12, R6.Pin_0
  N5: J1.pin13, R5.Pin_0
  N6: J1.pin14, R4.Pin_0
  N7: J4.pin1, U1.pin1
  N8: J4.pin2, U1.pin2
  N9: LED1.red_cathode, J5.pin1
  N10: LED1.common_anode, J5.pin2
  N11: LED1.green_cathode, J5.pin3
  N12: LED1.blue_cathode, J5.pin4
  N13: R4.Pin_1, R9.Pin_0, Q4.B
  N14: R5.Pin_1, R11.Pin_0, Q2.B
  N15: R6.Pin_1, R10.Pin_0, Q1.B
  N16: R8.Pin_1, Q3.B
  N17: R1.Pin_0, Q1.C
  N18: R1.Pin_1, J3.pin1
  N19: R2.Pin_0, Q2.C
  N20: R2.Pin_1, J3.pin3
  N21: R3.Pin_0, Q3.C
  N22: R3.Pin_1, J3.pin4

notes:
  LED vendor data:
  Red: 1.8-2.0V
  Green: 3.2-3.4V
  Blue: 3.2-3.4V
  Resistors determined from experiments with LED brightness
  Internal resistance of pins when in "IN" mode during boot is about 10k. Except for pin 10, where it's about 2.5k. So the odd one out gets to be the FET.
